# Fritzing sketch USB-Sanitizer-40pin (saved by Fritzing 0.9.2b)

parts:
  LED1 = smd LED [color="Red (633nm)" package="0603 [SMD]"]
  LED2 = smd LED [color="Orange (605nm)" package="0603 [SMD]"]
  R2 = Resistor [tolerance=±5% resistance=1k package=THT]
  R3 = Resistor [tolerance=±5% resistance=1k package=THT]
  LED3 = smd LED [color="Green (560nm)" package="0603 [SMD]"]
  R1 = Resistor [tolerance=±5% resistance=1k package=THT]
  S2 = SWITCH-MOMENTARY-2 [package=tactile-pth]
  S3 = SWITCH-MOMENTARY-2 [package=tactile-pth]
  Raspberry_Pi2 = Raspberry Pi B+
  R4 = Resistor [tolerance=±5% resistance=1k package=THT]
  LED4 = smd LED [color="Green (560nm)" package="0603 [SMD]"]
  R5 = Resistor [tolerance=±5% resistance=1k package=THT]
  R6 = Resistor [tolerance=±5% resistance=1k package=THT]
  LED5 = smd LED [color="Orange (605nm)" package="0603 [SMD]"]
  LED6 = smd LED [color="Red (633nm)" package="0603 [SMD]"]
  S4 = SWITCH-MOMENTARY-2 [package=tactile-pth]
  S5 = SWITCH-MOMENTARY-2 [package=tactile-pth]

nets:
  N1: LED1.cathode, LED2.cathode, LED3.cathode, S2.1, S3.1, Raspberry_Pi2.GND, LED4.cathode, LED5.cathode, LED6.cathode
  N2: R2.Pin_1, Raspberry_Pi2.GPIO8
  N3: R3.Pin_1, Raspberry_Pi2.GPIO25
  N4: R1.Pin_1, Raspberry_Pi2.GPIO7
  N5: S2.2, Raspberry_Pi2.GPIO3
  N6: S3.2, Raspberry_Pi2.GPIO17
  N7: Raspberry_Pi2.3V3, S5.2
  N8: Raspberry_Pi2.GPIO13, S4.1
  N9: Raspberry_Pi2.GPIO26, S5.1
  N10: Raspberry_Pi2.GPIO21, R4.Pin_1
  N11: Raspberry_Pi2.GPIO20, R6.Pin_1
  N12: Raspberry_Pi2.GPIO16, R5.Pin_1
