# Fritzing sketch USB-Sanitizer (saved by Fritzing 0.9.2b)

parts:
  Raspberry_Pi1 = Raspberry Pi B rev2
  LED1 = smd LED [color="Red (633nm)" package="0603 [SMD]"]  # not connected
  LED2 = smd LED [color="Orange (605nm)" package="0603 [SMD]"]  # not connected
  R2 = Resistor [tolerance=±5% resistance=1k package=THT]
  R3 = Resistor [tolerance=±5% resistance=1k package=THT]
  LED3 = smd LED [color="Green (560nm)" package="0603 [SMD]"]
  R1 = Resistor [tolerance=±5% resistance=1k package=THT]
  S2 = SWITCH-MOMENTARY-2 [package=tactile-pth]
  S3 = SWITCH-MOMENTARY-2 [package=tactile-pth]

nets:
  N1: Raspberry_Pi1.GPIO_3, S2.2
  N2: Raspberry_Pi1.GND, LED3.cathode, S2.1, S3.1
  N3: Raspberry_Pi1.GPIO_17, S3.2
  N4: Raspberry_Pi1.GPIO_25, R3.Pin_1
  N5: Raspberry_Pi1.GPIO_8, R2.Pin_1
  N6: Raspberry_Pi1.GPIO_7, R1.Pin_1
